# Fritzing sketch pi-pico-2led (saved by Fritzing 0.9.6b)
breadboards: 1

parts:
  A1 = Raspberry Pi Pico H
  S1 = Momentary Switch [package=tactile-pth]
  R1 = Resistor [tolerance=±5% power=0.25 resistance=220 package=THT]
  LED1 = LED - 5mm [color="Red (633nm)" current=0.030 package="5 mm [THT]"]

nets:
  N1: A1.GND, S1.2, R1.Pin_1
  N2: A1.GP15, LED1.cathode
  N3: A1.RUN, S1.3
  N4: R1.Pin_0, LED1.anode

custom parts:
  Raspberry Pi Pico H: Raspberry Pi Pico H. Based around the RP2040 microcontroller the Pico H is a low cost microcontroller device bringing Raspberry Pi quality, cost, and easy of use to the microcontroller space.
